# Fritzing sketch lighting_and_button (saved by Fritzing 0.8.3b)
breadboards: 1

parts:
  RF1 = nRF8001 Bluetooth LE Breakout
  Part1 = Arduino Uno (Rev3)
  LED1 = LED - 5mm [color="Red (633nm)" package="5 mm [THT]"]
  R1 = Resistor [tolerance=±5% resistance=220 package=THT]
  BUTTON1 = Arcade Button (white)
  R2 = Resistor [tolerance=±5% resistance=10k package=THT]

nets:
  N1: RF1.SCK, Part1.ICSP_SCK, Part1.D13/SCK
  N2: RF1.MISO, Part1.ICSP_MISO, Part1.D12/MISO
  N3: RF1.MOSI, Part1.ICSP_MOSI, Part1.D11_PWM/MOSI
  N4: RF1.REQ, Part1.D10_PWM/SS
  N5: RF1.RDY, Part1.D2
  N6: RF1.RST, Part1.D9_PWM
  GND: RF1.GND, Part1.GND, LED1.cathode, R2.Pin_1
  VIN: RF1.VIN, Part1.5V, BUTTON1.no_name_yet#2
  N7: Part1.D3_PWM, R1.Pin_1
  N8: Part1.D4, BUTTON1.no_name_yet#1, R2.Pin_0
  N9: LED1.anode, R1.Pin_0

custom parts:
  nRF8001 Bluetooth LE Breakout: nRF8001 Breakout Board
  Arcade Button (white): Adafruit Arcade Button (white)
