# Fritzing sketch circuit (saved by Fritzing 0.8.3b)
breadboards: 1

parts:
  Part1 = Arduino Uno (Rev3)
  R1 = Resistor [tolerance=±5% resistance=220 package=THT]
  LED1 = LED - 5mm [color="Red (633nm)" package="5 mm [THT]"]
  LED2 = LED - 5mm [color="Red (633nm)" package="5 mm [THT]"]
  R2 = Resistor [tolerance=±5% resistance=220 package=THT]

nets:
  N1: Part1.ICSP_MISO, Part1.D12/MISO, R2.Pin_0
  N2: Part1.ICSP_SCK, Part1.D13/SCK, R1.Pin_0
  N3: Part1.GND, LED1.anode
  N4: Part1.5V, LED2.anode
  N5: R1.Pin_1, LED1.cathode
  N6: LED2.cathode, R2.Pin_1
